// Logisim project Proyecto_Digital.circ as structural Verilog: 3 circuits, main circuit main
module main (
);

  wire [15:0] columnaaleatoria_1_out_1, obstaculo_1_out_2, obstaculo_1_out_3, obstaculo_1_out_4,
       obstaculo_1_out_5, obstaculo_1_out_6, obstaculo_1_out_7, obstaculo_1_out_8, obstaculo_1_out_9,
       obstaculo_1_out_10, obstaculo_1_out_11, obstaculo_1_out_12, obstaculo_1_out_13, obstaculo_1_out_14,
       obstaculo_1_out_15, obstaculo_1_out_16, obstaculo_1_out_17, obstaculo_1_out_18, obstaculo_1_out_19,
       obstaculo_1_out_20, obstaculo_1_out_21, obstaculo_1_out_22, obstaculo_1_out_23, obstaculo_1_out_24,
       obstaculo_1_out_25, obstaculo_1_out_26, obstaculo_1_out_27, obstaculo_1_out_28, obstaculo_1_out_29,
       obstaculo_1_out_30, obstaculo_1_out_31, obstaculo_1_out_32, obstaculo_1_out_33;

  Hex_Digit_Display hex_digit_display_1 ();  // open: value, dp
  Obstaculo obstaculo_1 (
    .out_2(obstaculo_1_out_2), .out_3(obstaculo_1_out_3), .out_4(obstaculo_1_out_4),
    .out_5(obstaculo_1_out_5), .out_6(obstaculo_1_out_6), .out_7(obstaculo_1_out_7),
    .out_8(obstaculo_1_out_8), .out_9(obstaculo_1_out_9), .out_10(obstaculo_1_out_10),
    .out_11(obstaculo_1_out_11), .out_12(obstaculo_1_out_12), .out_13(obstaculo_1_out_13),
    .out_14(obstaculo_1_out_14), .out_15(obstaculo_1_out_15), .out_16(obstaculo_1_out_16),
    .out_17(obstaculo_1_out_17), .out_18(obstaculo_1_out_18), .out_19(obstaculo_1_out_19),
    .out_20(obstaculo_1_out_20), .out_21(obstaculo_1_out_21), .out_22(obstaculo_1_out_22),
    .out_23(obstaculo_1_out_23), .out_24(obstaculo_1_out_24), .out_25(obstaculo_1_out_25),
    .out_26(obstaculo_1_out_26), .out_27(obstaculo_1_out_27), .out_28(obstaculo_1_out_28),
    .out_29(obstaculo_1_out_29), .out_30(obstaculo_1_out_30), .out_31(obstaculo_1_out_31),
    .out_32(obstaculo_1_out_32), .out_33(obstaculo_1_out_33), .in_1(columnaaleatoria_1_out_1));
  DotMatrix #(.inputtype("row"), .matrixcols(16), .matrixrows(32)) dotmatrix_1 (
    .row0(obstaculo_1_out_2), .row1(obstaculo_1_out_3), .row2(obstaculo_1_out_4), .row3(obstaculo_1_out_5),
    .row4(obstaculo_1_out_6), .row5(obstaculo_1_out_7), .row6(obstaculo_1_out_8), .row7(obstaculo_1_out_9),
    .row8(obstaculo_1_out_10), .row9(obstaculo_1_out_11), .row10(obstaculo_1_out_12),
    .row11(obstaculo_1_out_13), .row12(obstaculo_1_out_14), .row13(obstaculo_1_out_15),
    .row14(obstaculo_1_out_16), .row15(obstaculo_1_out_17), .row16(obstaculo_1_out_18),
    .row17(obstaculo_1_out_19), .row18(obstaculo_1_out_20), .row19(obstaculo_1_out_21),
    .row20(obstaculo_1_out_22), .row21(obstaculo_1_out_23), .row22(obstaculo_1_out_24),
    .row23(obstaculo_1_out_25), .row24(obstaculo_1_out_26), .row25(obstaculo_1_out_27),
    .row26(obstaculo_1_out_28), .row27(obstaculo_1_out_29), .row28(obstaculo_1_out_30),
    .row29(obstaculo_1_out_31), .row30(obstaculo_1_out_32), .row31(obstaculo_1_out_33));
  ColumnaAleatoria columnaaleatoria_1 (.out_1(columnaaleatoria_1_out_1));
  Hex_Digit_Display hex_digit_display_2 ();  // open: value, dp
endmodule

module Obstaculo (
  input  [15:0] in_1,
  output [15:0] out_2,
  output [15:0] out_3,
  output [15:0] out_4,
  output [15:0] out_5,
  output [15:0] out_6,
  output [15:0] out_7,
  output [15:0] out_8,
  output [15:0] out_9,
  output [15:0] out_10,
  output [15:0] out_11,
  output [15:0] out_12,
  output [15:0] out_13,
  output [15:0] out_14,
  output [15:0] out_15,
  output [15:0] out_16,
  output [15:0] out_17,
  output [15:0] out_18,
  output [15:0] out_19,
  output [15:0] out_20,
  output [15:0] out_21,
  output [15:0] out_22,
  output [15:0] out_23,
  output [15:0] out_24,
  output [15:0] out_25,
  output [15:0] out_26,
  output [15:0] out_27,
  output [15:0] out_28,
  output [15:0] out_29,
  output [15:0] out_30,
  output [15:0] out_31,
  output [15:0] out_32,
  output [15:0] out_33
);

  wire clock_1_out;

  Clock clock_1 (.out(clock_1_out));
  Register #(.width(16)) register_1 (.D(in_1), .Q(out_2), .clk(clock_1_out));  // open: en, clr
  Register #(.width(16)) register_2 (.D(out_9), .Q(out_10), .clk(clock_1_out));  // open: en, clr
  Register #(.width(16)) register_3 (.D(out_17), .Q(out_18), .clk(clock_1_out));  // open: en, clr
  Register #(.width(16)) register_4 (.D(out_25), .Q(out_26), .clk(clock_1_out));  // open: en, clr
  Register #(.width(16), .trigger("high")) register_5 (.D(out_2), .Q(out_3), .clk(clock_1_out));  // open: en, clr
  Register #(.width(16), .trigger("high")) register_6 (.D(out_10), .Q(out_11), .clk(clock_1_out));  // open: en, clr
  Register #(.width(16), .trigger("high")) register_7 (.D(out_18), .Q(out_19), .clk(clock_1_out));  // open: en, clr
  Register #(.width(16), .trigger("high")) register_8 (.D(out_26), .Q(out_27), .clk(clock_1_out));  // open: en, clr
  Register #(.width(16)) register_9 (.D(out_3), .Q(out_4), .clk(clock_1_out));  // open: en, clr
  Register #(.width(16)) register_10 (.D(out_11), .Q(out_12), .clk(clock_1_out));  // open: en, clr
  Register #(.width(16)) register_11 (.D(out_19), .Q(out_20), .clk(clock_1_out));  // open: en, clr
  Register #(.width(16)) register_12 (.D(out_27), .Q(out_28), .clk(clock_1_out));  // open: en, clr
  Register #(.width(16), .trigger("high")) register_13 (.D(out_4), .Q(out_5), .clk(clock_1_out));  // open: en, clr
  Register #(.width(16), .trigger("high")) register_14 (.D(out_12), .Q(out_13), .clk(clock_1_out));  // open: en, clr
  Register #(.width(16), .trigger("high")) register_15 (.D(out_20), .Q(out_21), .clk(clock_1_out));  // open: en, clr
  Register #(.width(16), .trigger("high")) register_16 (.D(out_28), .Q(out_29), .clk(clock_1_out));  // open: en, clr
  Register #(.width(16)) register_17 (.D(out_5), .Q(out_6), .clk(clock_1_out));  // open: en, clr
  Register #(.width(16)) register_18 (.D(out_13), .Q(out_14), .clk(clock_1_out));  // open: en, clr
  Register #(.width(16)) register_19 (.D(out_21), .Q(out_22), .clk(clock_1_out));  // open: en, clr
  Register #(.width(16)) register_20 (.D(out_29), .Q(out_30), .clk(clock_1_out));  // open: en, clr
  Register #(.width(16), .trigger("high")) register_21 (.D(out_6), .Q(out_7), .clk(clock_1_out));  // open: en, clr
  Register #(.width(16), .trigger("high")) register_22 (.D(out_14), .Q(out_15), .clk(clock_1_out));  // open: en, clr
  Register #(.width(16), .trigger("high")) register_23 (.D(out_22), .Q(out_23), .clk(clock_1_out));  // open: en, clr
  Register #(.width(16), .trigger("high")) register_24 (.D(out_30), .Q(out_31), .clk(clock_1_out));  // open: en, clr
  Register #(.width(16)) register_25 (.D(out_7), .Q(out_8), .clk(clock_1_out));  // open: en, clr
  Register #(.width(16)) register_26 (.D(out_15), .Q(out_16), .clk(clock_1_out));  // open: en, clr
  Register #(.width(16)) register_27 (.D(out_23), .Q(out_24), .clk(clock_1_out));  // open: en, clr
  Register #(.width(16)) register_28 (.D(out_31), .Q(out_32), .clk(clock_1_out));  // open: en, clr
  Register #(.width(16), .trigger("high")) register_29 (.D(out_8), .Q(out_9), .clk(clock_1_out));  // open: en, clr
  Register #(.width(16), .trigger("high")) register_30 (.D(out_16), .Q(out_17), .clk(clock_1_out));  // open: en, clr
  Register #(.width(16), .trigger("high")) register_31 (.D(out_24), .Q(out_25), .clk(clock_1_out));  // open: en, clr
  Register #(.width(16), .trigger("high")) register_32 (.D(out_32), .Q(out_33), .clk(clock_1_out));  // open: en, clr

  // Other names for the same wires on the sheet: _1[15:0] = out_2; _2[15:0] = out_3; _3[15:0] = out_4;
  //   _4[15:0] = out_5; _5[15:0] = out_6; _6[15:0] = out_7; _7[15:0] = out_8; _8[15:0] = out_9; _9[15:0] = out_10;
  //   _10[15:0] = out_11; _11[15:0] = out_12; _12[15:0] = out_13; _13[15:0] = out_14; _14[15:0] = out_15;
  //   _15[15:0] = out_16; _16[15:0] = out_17; _17[15:0] = out_18; _18[15:0] = out_19; _19[15:0] = out_20;
  //   _20[15:0] = out_21; _21[15:0] = out_22; _22[15:0] = out_23; _23[15:0] = out_24; _24[15:0] = out_25;
  //   _25[15:0] = out_26; _26[15:0] = out_27; _27[15:0] = out_28; _28[15:0] = out_29; _29[15:0] = out_30;
  //   _30[15:0] = out_31; _31[15:0] = out_32; _32[15:0] = out_33
endmodule

module ColumnaAleatoria (
  output [15:0] out_1
);

  wire clock_1_out, shift_register_1_out, shift_register_2_out;
  wire [3:0] Random;
  wire [15:0] multiplexer_1_out;

  Clock clock_1 (.out(clock_1_out));
  Random #(.width(4)) random_1 (.clk(clock_1_out), .out(Random));  // open: next, clr
  Shift_Register #(.length(16)) shift_register_1 (
    .in(1'b1), .clk(clock_1_out), .out(shift_register_1_out), .clr(shift_register_1_out));  // open: shift, load, d0, q0, d1, q1, d2, q2, d3, q3, d4, q4, d5, q5, d6, q6, d7, q7, d8, q8, d9, q9, d10, q10, d11, q11, d12, q12, d13, q13, d14, q14, d15, q15
  Multiplexer #(.select(4), .width(16)) multiplexer_1 (
    .in0(16'hc000), .in1(16'h6000), .in2(16'h3000), .in3(16'h1800), .in4(16'hc00), .in5(16'h600),
    .in6(16'h300), .in7(16'h180), .in8(16'hc0), .in9(16'h60), .in10(16'h30), .in11(16'h18), .in12(16'hc),
    .in13(16'h6), .in14(16'h3), .in15(16'h3), .out(multiplexer_1_out), .sel(Random));  // open: en
  Shift_Register #(.length(1)) shift_register_2 (
    .in(1'b1), .clk(clock_1_out), .out(shift_register_2_out), .clr(shift_register_1_out));  // open: shift, load, d0, q0
  Multiplexer #(.width(16)) multiplexer_2 (
    .in0(multiplexer_1_out), .in1({16{1'b0}}), .out(out_1), .sel(shift_register_2_out));  // open: en

  // Notes on the sheet:
  //   Output random del MUX
  //   valores random hexadecimales de 1100.. a ..0011
  //   Input del circuito obstaculo, pixel que iniciara efecto cascada
endmodule
